# Fritzing sketch Simulador-Conexiones (saved by Fritzing 0.9.10b)
breadboards: 1

parts:
  Mod1 = Heltec WiFi LoRa 32 V2 [part_number=HTIT-WB32LA]
  LCD1 = LCD screen
  J1 = Basic Servo
  J2 = Basic Servo
  R1 = Rotary Potentiometer (Small) [maximum_resistance=100kΩ knob_status=50% power=0.5W package=THT]
  GM1 = GM67 Barcode Reader
  Mod2 = KY-003 Hall Magnetic Sensor Module [package="Breakout board"]
  J3 = ATX24 Pin Power Supply Connector [package=atx24_right_angle]
  R2 = Resistor [tolerance=±5% resistance=220 package="0805 [SMD]"]
  R3 = Resistor [tolerance=±5% resistance=220 package="0805 [SMD]"]
  R4 = Resistor [tolerance=±5% resistance=220 package="0805 [SMD]"]

nets:
  N1: Mod1.pin_2, LCD1.DB7
  N2: Mod1.pin_3, LCD1.DB6
  N3: Mod1.pin_4, LCD1.DB5
  N4: Mod1.pin_5, LCD1.DB4
  N5: Mod1.pin_11, LCD1.E
  N6: Mod1.pin_12, LCD1.RS
  GND: Mod1.GND, LCD1.VSS, LCD1.LED-, J1.gnd, J2.gnd, R1.leg2, GM1.GND, Mod2.-
  N7: Mod1.pin_20, R2.Pin_0, R4.Pin_1
  N8: Mod1.pin_26, GM1.RX
  N9: Mod1.pin_27, GM1.TX
  N10: Mod1.pin_32, J1.pulse, J2.pulse
  N11: Mod1.pin_35, Mod2.S
  VCC: LCD1.VDD, J1.vcc, J2.vcc, GM1.5V, J3.5V, R3.Pin_0
  N12: LCD1.V0, R1.wiper
  N13: LCD1.LED+, R4.Pin_0
  N14: R1.leg1, R2.Pin_1
  N15: Mod2.Vin, R3.Pin_1

custom parts:
  GM67 Barcode Reader: Header 8 GM67 Barcode Reader V1.0. Please ignore the PCB view of this circuit it does not matter. Please feel free to make this better
  KY-003 Hall Magnetic Sensor Module: KEYES KY-003 Arduino Hall Magnetic Sensor Module is a switch that will turn on/off in the presence of a magnetic field.
